# Fritzing sketch wiring_diagram (saved by Fritzing 0.9.3b)

parts:
  M1 = MKR ZERO
  A1 = GT-U7 NEO6M GPS
  BAT1 = Battery Holders [package=lipo-1100mAh]

nets:
  N1: M1.D13_RX, A1.Pin_2
  N2: M1.14_TX, A1.Pin_3
  N3: M1.GND, M1.-VBAT, A1.Pin_4, BAT1.-
  N4: M1.VCC, A1.Pin_5, BAT1.+

custom parts:
  MKR ZERO: arduino mrk zero SAMD21 Cortex-M0+ 32bit low power ARM MCU 256 meg flash 32kb sram 48mhz
  GT-U7 NEO6M GPS: GT-U7 NEO6M GPS.
